# Fritzing sketch contador pulsos (saved by Fritzing 0.9.3b)
breadboards: 1

parts:
  Componente1 = Arduino Uno (Rev3)
  S1 = Round Pushbutton
  Componente2 = Adafruit I2C+SPI LCD Backpack [part_number="Adafruit #292"]
  LCD1 = LCD screen
  R1 = Resistor [tolerance=±5% resistance=220 package="1206 [SMD]"]

nets:
  N1: Componente1.A4/SDA, Componente2.DATA
  N2: Componente1.A5/SCL, Componente2.CLOCK
  N3: Componente1.D3_PWM, S1.leg0, R1.Pin_1
  5V: Componente1.5V, Componente2.VCC, LCD1.VDD, R1.Pin_0
  GND: Componente1.GND, S1.leg1, Componente2.GND, LCD1.VSS, LCD1.R/W
  N4: Componente2.CONTRAST, LCD1.V0
  N5: Componente2.RS, LCD1.RS
  N6: Componente2.E, LCD1.E
  N7: Componente2.DB0, LCD1.DB0
  N8: Componente2.DB1, LCD1.DB1
  N9: Componente2.DB2, LCD1.DB2
  N10: Componente2.DB3, LCD1.DB3

custom parts:
  Adafruit I2C+SPI LCD Backpack: LCD backpacks reduce the number of pins needed to connect to an LCD. LCDs are a fun and easy way to have your microcontroller project talk back to you. Character LCDs are common, and easy to get, available in tons of colors and sizes. We've written tutorials on using character LCDs with an Arduino (or similar microcontroller) but find that the number of pins necessary to control the LCD can be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
